# Fritzing sketch Gerenciamento de Energia em Fábricas Usando IoT (saved by Fritzing 0.9.3b)
breadboards: 2

parts:
  U1 = ESP32-38PinWide [part_number=ESP32-38PinWide]
  BAT1 = BC9VPC [package=bc9vpc]
  U3 = POT [package=pot_mammoth]
  KY-1 = Keyes Relay [package=THT]
  LED1 = LEDs [package=led10mm]
  R1 = Resistor [tolerance=±5% resistance=1k package="0603 [SMD]"]
  Componente1 = Arduino Nano (Rev3.0)
  R2 = Resistor [tolerance=±5% resistance=220 package=THT]
  LED2 = smd LED [color="Blue (525nm)" package="1206 [SMD]"]

nets:
  VIN: U1.VIN, Componente1.5V
  N1: U1.GPIO3, Componente1.D1/TX
  N2: U1.GPIO1, Componente1.D0/RX
  GND: U1.GND, BAT1.V-, U3.S, KY-1.ground, LED1.C, Componente1.GND, LED2.cathode
  N3: BAT1.V+, U3.E
  N4: U3.A, R1.Pin_0, Componente1.A7, R2.Pin_0
  N5: KY-1.signal, Componente1.D2
  N6: KY-1.power, Componente1.3V3
  N7: KY-1.C, R2.Pin_1
  N8: KY-1.NO, LED2.anode
  N9: LED1.A, R1.Pin_1

custom parts:
  ESP32-38PinWide: Generic 38-Pin ESP32 with wide format (only access to one side of pins on a breadboard) based on Stephen Lilley's HiLetgo ESP-WROOM-32 ESP32 ESP-32S Development Board.
  Keyes Relay: The Keyes 5V relay module is suitable for SCM development, home appliance control. It uses a 5V~12V TIL control signal which can control DC / AC signal.

// code stored in the sketch: ProjetoObjetos.ino
int cor = A7;        // Porta A0 para ler a corrente
int tomada1 = 2;
float I = 0;         // Variável para leitura do valor analógico
float corrente = 0.0;// Variável para armazenar a corrente convertida (em mA)
int valorPWM = 0;    // Variável para armazenar o valor de saída PWM


void setup() {
    Serial.begin(9600);           // Inicializa a comunicação serial
    pinMode(tomada1, OUTPUT);     // Define a porta como saída
}


void loop() {
  I = analogRead(cor);  // Lê o valor do sensor de corrente na porta A0
  
  // Calcula a corrente em mA
  corrente = (I * 5.0) / 1024.0;
  
  Serial.print("Corrente: ");
  Serial.print(corrente);
  Serial.println(" mA");


  // Verifica se a corrente está acima de 4.0 mA
  if (corrente > 4.8) {
    digitalWrite(tomada1, HIGH);
  } else {
    digitalWrite(tomada1, LOW);
  }
}
